// Digital circuit 8_Bit_Harvard_CPU_1.dig as structural Verilog
module _8_Bit_Harvard_CPU_1 (
  input  CALC,
  input  CLR,
  input  in_3,
  input  in_4,
  input  in_5,
  input  SHR,
  input  SHL,
  input  HOLD_LD,
  input  CLR_2,
  input  nOE,
  input  LOAD,
  input  INC,
  input  DEP,
  input  in_14,
  input  in_15,
  input  in_16,
  input  in_17,
  input  in_18,
  input  HOLD_LD_2,
  input  CLR_3,
  input  nOE_2,
  input  CK,
  input  clk,
  input  CALC_2,
  input  CLR_4,
  input  in_26,
  input  in_27,
  input  in_28,
  input  SHR_2,
  input  SHL_2
);

  wire _7425_1_pin6, _7425_2_pin6, _74173_1_pin3, _74173_1_pin4, _74173_1_pin5, _74173_1_pin6, _74173_2_pin3,
       _74173_2_pin4, _74173_2_pin5, _74173_2_pin6, AC0, AC1, AC2, AC3, AC4, AC5, AC6, AC7, AL, ALU0, ALU1,
       ALU2, ALU3, ALU4, ALU5, ALU6, ALU7, AR0, AR1, AR2, AR3, BUS0, BUS1, BUS2, BUS3, BUS4, BUS5, BUS6,
       BUS7, button_7_out, C1, CLK2, CO, D0, D1, D2, D3, D4, D5, D6, D7, diodebackward_1_out,
       diodebackward_5_out, diodebackward_7_out, diodebackward_9_out, diodebackward_27_out, EH, EL, IC1_pin2,
       IC1_pin3, IC1_pin8, IC2_pin2, IC2_pin3, IC2_pin8, IC2_pin11, IC3_pin2, IC3_pin3, IC3_pin8, IC3_pin11,
       IC4_pin1, IC4_pin2, IC4_pin3, IC4_pin8, IC4_pin11, IC7_pin7, IC7_pin9, IC8_pin7, IC8_pin9, IC9_pin7,
       IC9_pin9, IC10_pin7, IC10_pin9, IC16_pin10, IC18_pin9, IC18_pin10, IC18_pin11, IC18_pin12, IC18_pin13,
       IC18_pin14, IC18_pin15, IC19_pin7, IC19_pin9, IC19_pin10, IC19_pin11, IC19_pin12, IC19_pin13,
       IC19_pin14, IC19_pin15, IC20_pin7, IC20_pin9, IC20_pin12, IC20_pin13, IC20_pin14, IC20_pin15,
       IC22_pin7, IC23_2_pin7, IC23_2_pin9, IC23_pin15, IC24_2_pin7, IC24_2_pin9, IC24_pin11, IC24_pin12,
       IC24_pin13, IC24_pin14, IC24_pin15, IC25_2_pin7, IC25_2_pin9, IC25_pin11, IC25_pin12, IC25_pin13,
       IC25_pin14, IC25_pin15, IC26_2_pin7, IC26_2_pin9, IC26_pin11, IC26_pin12, IC26_pin13, IC26_pin14,
       IC27_p9, IC27_p10, IC27_p11, IC27_p12, IC27_p13, IC27_p15, IC27_p16, IC27_p17, IC27_p18, IC27_p19,
       IC27_p20, IC27_p21, IC27_p22, IC28_pin2, IC28_pin3, IC28_pin4, IR0, IR1, IR2, IR3, IR4, IR5, IR6, IX,
       nAE, nBF, nDE, nIE, nJMP, nLD, nOE_t, nOL, not_1_out, not_3_out, nPH, nPL, nWE, nXL, nYL,
       pullup_6_out, pullup_8_out, reset_1_out;
  wire [3:0] IC4_pin9, IC12S_2_pin15, IC12S_pin15, IC13_pin4, IC13_pin13, IC14_pin6, IC15_pin14, IC16_pin11,
       IC23_pin11;

  _7474 IC4 (
    .pin1(IC4_pin1), .pin2(IC4_pin2), .pin3(IC4_pin3), .pin4(1'b1), .pin5(IC4_pin9[3]), .pin6(IC4_pin2),
    .pin7(1'b0), .pin8(IC4_pin8), .pin9(IC4_pin9[2]), .pin10(1'b1), .pin11(IC4_pin11), .pin12(IC4_pin8),
    .pin13(IC4_pin1), .pin14(1'b1));
  Button #(.activeLow("true")) CLEAR (.out(IC4_pin1));
  _74173 IC14 (
    .pin1(nOE), .pin2(nOE), .pin3(IC14_pin6[0]), .pin4(IC14_pin6[1]), .pin5(IC14_pin6[2]),
    .pin6(IC14_pin6[3]), .pin7(DEP), .pin8(1'b0), .pin9(HOLD_LD), .pin10(HOLD_LD), .pin11(IC4_pin9[3]),
    .pin12(IC4_pin9[2]), .pin13(IC4_pin9[1]), .pin14(IC4_pin9[0]), .pin15(CLR_2), .pin16(1'b1));
  _74173 IC13 (
    .pin1(nOE), .pin2(nOE), .pin3(IC13_pin4[0]), .pin4(IC13_pin4[1]), .pin5(IC13_pin4[2]),
    .pin6(IC13_pin4[3]), .pin7(DEP), .pin8(1'b0), .pin9(HOLD_LD), .pin10(HOLD_LD), .pin11(IC13_pin13[2]),
    .pin12(IC13_pin13[3]), .pin13(IC13_pin13[1]), .pin14(IC13_pin13[0]), .pin15(CLR_2), .pin16(1'b1));
  LED led_1 (.in(IC4_pin9[3]));
  _7474 IC3 (
    .pin1(IC4_pin1), .pin2(IC3_pin2), .pin3(IC3_pin3), .pin4(1'b1), .pin5(IC4_pin9[0]), .pin6(IC3_pin2),
    .pin7(1'b0), .pin8(IC3_pin8), .pin9(IC4_pin9[1]), .pin10(1'b1), .pin11(IC3_pin11), .pin12(IC3_pin8),
    .pin13(IC4_pin1), .pin14(1'b1));
  Button button_1 (.out(IC4_pin3));
  Seven_Seg_Hex seven_seg_hex_1 (.d(IC14_pin6), .dp(1'b0));
  LED led_2 (.in(IC4_pin9[2]));
  Button button_2 (.out(IC4_pin11));
  Seven_Seg_Hex seven_seg_hex_2 (.d(IC13_pin4), .dp(1'b0));
  LED led_3 (.in(IC4_pin9[1]));
  Button button_3 (.out(IC3_pin11));
  _74163 IC16 (
    .pin1(1'b1), .pin2(DEP), .pin3(IC14_pin6[0]), .pin4(IC14_pin6[1]), .pin5(IC14_pin6[2]),
    .pin6(IC14_pin6[3]), .pin7(1'b1), .pin8(1'b0), .pin9(LOAD), .pin10(IC16_pin10), .pin11(IC16_pin11[3]),
    .pin12(IC16_pin11[2]), .pin13(IC16_pin11[1]), .pin14(IC16_pin11[0]), .pin16(1'b1));  // open: pin15
  LED led_4 (.in(IC4_pin9[0]));
  _7474 IC2 (
    .pin1(IC4_pin1), .pin2(IC2_pin2), .pin3(IC2_pin3), .pin4(1'b1), .pin5(IC13_pin13[3]), .pin6(IC2_pin2),
    .pin7(1'b0), .pin8(IC2_pin8), .pin9(IC13_pin13[2]), .pin10(1'b1), .pin11(IC2_pin11), .pin12(IC2_pin8),
    .pin13(IC4_pin1), .pin14(1'b1));
  Button button_4 (.out(IC3_pin3));
  Delay #(.delayTime(2)) delay_1 (.in(clk), .out(CLK2));
  LED led_5 (.in(IC13_pin13[3]));
  Button button_5 (.out(IC2_pin3));
  _74173 _74173_1 (
    .pin1(1'b0), .pin2(1'b0), .pin3(_74173_1_pin3), .pin4(_74173_1_pin4), .pin5(_74173_1_pin5),
    .pin6(_74173_1_pin6), .pin7(CLK2), .pin8(1'b0), .pin9(nYL), .pin10(nYL), .pin11(ALU0), .pin12(ALU1),
    .pin13(ALU2), .pin14(ALU3), .pin15(1'b0), .pin16(1'b1));
  _74173 _74173_2 (
    .pin1(1'b0), .pin2(1'b0), .pin3(_74173_2_pin3), .pin4(_74173_2_pin4), .pin5(_74173_2_pin5),
    .pin6(_74173_2_pin6), .pin7(CLK2), .pin8(1'b0), .pin9(nYL), .pin10(nYL), .pin11(ALU4), .pin12(ALU5),
    .pin13(ALU6), .pin14(ALU7), .pin15(1'b0), .pin16(1'b1));
  LED led_6 (.in(IC13_pin13[2]));
  Button button_6 (.out(IC2_pin11));
  Reset reset_1 (.out(reset_1_out));
  Seven_Seg_Hex seven_seg_hex_3 (.d(IC16_pin11), .dp(1'b0));
  LED led_7 (.in(IC13_pin13[1]));
  Button button_7 (.out(button_7_out));
  Seven_Seg_Hex seven_seg_hex_4 (.d(IC15_pin14), .dp(1'b0));
  _7474 IC1 (
    .pin1(IC4_pin1), .pin2(IC1_pin2), .pin3(IC1_pin3), .pin4(1'b1), .pin5(IC13_pin13[0]), .pin6(IC1_pin2),
    .pin7(1'b0), .pin8(IC1_pin8), .pin9(IC13_pin13[1]), .pin10(1'b1), .pin11(button_7_out), .pin12(IC1_pin8),
    .pin13(IC4_pin1), .pin14(1'b1));
  Seven_Seg_Hex seven_seg_hex_5 (.d(IC4_pin9), .dp(1'b0));
  LED led_8 (.in(IC13_pin13[0]));
  Button button_8 (.out(IC1_pin3));
  _74163 IC23 (
    .pin1(reset_1_out), .pin2(clk), .pin3(BUS0), .pin4(BUS1), .pin5(BUS2), .pin6(BUS3), .pin7(1'b1),
    .pin8(1'b0), .pin9(nPL), .pin10(1'b1), .pin11(IC23_pin11[3]), .pin12(IC23_pin11[2]),
    .pin13(IC23_pin11[1]), .pin14(IC23_pin11[0]), .pin15(IC23_pin15), .pin16(1'b1));
  _74163 IC24 (
    .pin1(reset_1_out), .pin2(clk), .pin3(BUS4), .pin4(BUS5), .pin5(BUS6), .pin6(BUS7), .pin7(1'b1),
    .pin8(1'b0), .pin9(nPL), .pin10(IC23_pin15), .pin11(IC24_pin11), .pin12(IC24_pin12), .pin13(IC24_pin13),
    .pin14(IC24_pin14), .pin15(IC24_pin15), .pin16(1'b1));
  _74163 IC25 (
    .pin1(reset_1_out), .pin2(clk), .pin3(_74173_1_pin6), .pin4(_74173_1_pin5), .pin5(_74173_1_pin4),
    .pin6(_74173_1_pin3), .pin7(1'b1), .pin8(1'b0), .pin9(nPH), .pin10(IC24_pin15), .pin11(IC25_pin11),
    .pin12(IC25_pin12), .pin13(IC25_pin13), .pin14(IC25_pin14), .pin15(IC25_pin15), .pin16(1'b1));
  _74163 IC26 (
    .pin1(reset_1_out), .pin2(clk), .pin3(_74173_2_pin6), .pin4(_74173_2_pin5), .pin5(_74173_2_pin4),
    .pin6(_74173_2_pin3), .pin7(1'b1), .pin8(1'b0), .pin9(nPH), .pin10(IC25_pin15), .pin11(IC26_pin11),
    .pin12(IC26_pin12), .pin13(IC26_pin13), .pin14(IC26_pin14), .pin16(1'b1));  // open: pin15
  _74163 IC15 (
    .pin1(1'b1), .pin2(DEP), .pin3(IC13_pin4[0]), .pin4(IC13_pin4[1]), .pin5(IC13_pin4[2]),
    .pin6(IC13_pin4[3]), .pin7(1'b1), .pin8(1'b0), .pin9(LOAD), .pin10(1'b1), .pin11(IC15_pin14[3]),
    .pin12(IC15_pin14[2]), .pin13(IC15_pin14[1]), .pin14(IC15_pin14[0]), .pin15(IC16_pin10), .pin16(1'b1));
  Seven_Seg_Hex seven_seg_hex_6 (.d(IC13_pin13), .dp(1'b0));
  // A623308A IC17: pin names not known; wires that end beside it: in_14, IC16_pin11[3], IC16_pin11[2], IC16_pin11[1], IC16_pin11[0], IC15_pin14[3], IC15_pin14[2], IC15_pin14[1], IC15_pin14[0], BUS0, BUS1, BUS2, 1'b0, 1'b1, nWE, in_15, in_16, in_17, nOE_t, in_18, 1'b0, BUS7
  _74173 IC6 (
    .pin1(nOE_2), .pin2(nOE_2), .pin3(BUS4), .pin4(BUS5), .pin5(BUS6), .pin6(BUS7), .pin7(CK), .pin8(1'b0),
    .pin9(HOLD_LD_2), .pin10(HOLD_LD_2), .pin11(IC4_pin9[3]), .pin12(IC4_pin9[2]), .pin13(IC4_pin9[1]),
    .pin14(IC4_pin9[0]), .pin15(CLR_3), .pin16(1'b1));
  _74173 IC5 (
    .pin1(nOE_2), .pin2(nOE_2), .pin3(BUS0), .pin4(BUS1), .pin5(BUS2), .pin6(BUS3), .pin7(CK), .pin8(1'b0),
    .pin9(HOLD_LD_2), .pin10(HOLD_LD_2), .pin11(IC13_pin13[3]), .pin12(IC13_pin13[2]), .pin13(IC13_pin13[1]),
    .pin14(IC13_pin13[0]), .pin15(CLR_3), .pin16(1'b1));
  Seven_Seg_Hex seven_seg_hex_7 (.d(IC23_pin11), .dp(1'b0));
  Seven_Seg_Hex seven_seg_hex_8 (.d({BUS7, BUS6, BUS5, BUS4}), .dp(1'b0));
  // _27C1024 IC27: pin names not known; wires that end beside it: IC25_pin13, IC25_pin12, IC25_pin11, IC26_pin14, IC26_pin13, IC26_pin12, IC26_pin11, 1'b1, IC27_p9, IC27_p10, IC27_p11, IC27_p12, IC27_p13, 1'b0, IC27_p15, IC27_p16, IC27_p17, IC27_p18, IC27_p19, IC27_p20, IC27_p21, IC27_p22, 1'b0, 1'b1
  Seven_Seg_Hex seven_seg_hex_9 (.d({BUS3, BUS2, BUS1, BUS0}), .dp(1'b0));
  _74574 IC28 (
    .pin1(1'b0), .pin2(IC28_pin2), .pin3(IC28_pin3), .pin4(IC28_pin4), .pin5(IC27_p9), .pin6(IC27_p10),
    .pin7(IC27_p11), .pin8(IC27_p12), .pin9(IC27_p13), .pin10(1'b0), .pin11(clk), .pin12(1'b0), .pin13(IR6),
    .pin14(IR5), .pin15(IR4), .pin16(IR3), .pin17(IR2), .pin18(IR1), .pin19(IR0), .pin20(1'b1));
  _74574 IC29 (
    .pin1(1'b0), .pin2(IC27_p15), .pin3(IC27_p16), .pin4(IC27_p17), .pin5(IC27_p18), .pin6(IC27_p19),
    .pin7(IC27_p20), .pin8(IC27_p21), .pin9(IC27_p22), .pin10(1'b0), .pin11(clk), .pin12(D7), .pin13(D6),
    .pin14(D5), .pin15(D4), .pin16(D3), .pin17(D2), .pin18(D1), .pin19(D0), .pin20(1'b1));
  _74541 IC30 (
    .pin1(nDE), .pin2(D0), .pin3(D1), .pin4(D2), .pin5(D3), .pin6(D4), .pin7(D5), .pin8(D6), .pin9(D7),
    .pin10(1'b0), .pin11(BUS7), .pin12(BUS6), .pin13(BUS5), .pin14(BUS4), .pin15(BUS3), .pin16(BUS2),
    .pin17(BUS1), .pin18(BUS0), .pin19(nDE), .pin20(1'b1));
  _74153 IC22 (
    .pin1(nJMP), .pin2(CO), .pin3(1'b0), .pin4(IR4), .pin5(IR3), .pin6(IR2), .pin7(IC22_pin7), .pin8(1'b0),
    .pin10(1'b1), .pin11(1'b1), .pin12(1'b1), .pin13(1'b1), .pin14(AC7), .pin15(1'b1), .pin16(1'b1));  // open: pin9
  _74139 IC21 (
    .pin1(1'b0), .pin2(IR0), .pin3(IR1), .pin4(nDE), .pin5(nOE_t), .pin6(nAE), .pin7(nIE), .pin8(1'b0),
    .pin12(nBF), .pin13(IR2), .pin14(IR3), .pin15(IR4), .pin16(1'b1));  // open: pin9, pin10, pin11
  _74138 IC20 (
    .pin1(IR2), .pin2(IR3), .pin3(IR4), .pin4(1'b0), .pin5(1'b0), .pin6(1'b1), .pin7(IC20_pin7), .pin8(1'b0),
    .pin9(IC20_pin9), .pin10(nYL), .pin11(nXL), .pin12(IC20_pin12), .pin13(IC20_pin13), .pin14(IC20_pin14),
    .pin15(IC20_pin15), .pin16(1'b1));
  _74138 IC18 (
    .pin1(IR4), .pin2(IR5), .pin3(IR6), .pin4(1'b0), .pin5(1'b0), .pin6(1'b1), .pin7(nJMP), .pin8(1'b0),
    .pin9(IC18_pin9), .pin10(IC18_pin10), .pin11(IC18_pin11), .pin12(IC18_pin12), .pin13(IC18_pin13),
    .pin14(IC18_pin14), .pin15(IC18_pin15), .pin16(1'b1));
  _74138 IC19 (
    .pin1(IR4), .pin2(IR5), .pin3(IR6), .pin4(1'b0), .pin5(1'b0), .pin6(1'b0), .pin7(IC19_pin7), .pin8(1'b0),
    .pin9(IC19_pin9), .pin10(IC19_pin10), .pin11(IC19_pin11), .pin12(IC19_pin12), .pin13(IC19_pin13),
    .pin14(IC19_pin14), .pin15(IC19_pin15), .pin16(1'b1));
  DiodeBackward diodebackward_1 (.in(IC20_pin15), .out(diodebackward_1_out));
  DiodeBackward diodebackward_2 (.in(IC20_pin14), .out(diodebackward_1_out));
  DiodeBackward diodebackward_3 (.in(IC20_pin13), .out(diodebackward_1_out));
  DiodeBackward diodebackward_4 (.in(IC20_pin12), .out(diodebackward_1_out));
  DiodeBackward diodebackward_5 (.in(IR6), .out(diodebackward_5_out));
  DiodeBackward diodebackward_6 (.in(nJMP), .out(diodebackward_5_out));
  not not_1 (not_1_out, IC22_pin7);
  PullUp pullup_1 (.out(diodebackward_1_out));
  DiodeBackward diodebackward_7 (.in(IC20_pin9), .out(diodebackward_7_out));
  DiodeBackward diodebackward_8 (.in(IC20_pin7), .out(diodebackward_7_out));
  PullUp pullup_2 (.out(diodebackward_5_out));
  DiodeBackward diodebackward_9 (.in(IC18_pin15), .out(diodebackward_9_out));
  DiodeBackward diodebackward_10 (.in(IC18_pin14), .out(diodebackward_9_out));
  DiodeBackward diodebackward_11 (.in(IC18_pin13), .out(diodebackward_9_out));
  DiodeBackward diodebackward_12 (.in(IC18_pin11), .out(diodebackward_9_out));
  PullUp pullup_3 (.out(diodebackward_7_out));
  PullUp pullup_4 (.out(EL));
  DiodeBackward diodebackward_13 (.in(IC20_pin14), .out(EL));
  DiodeBackward diodebackward_14 (.in(IC20_pin12), .out(EL));
  DiodeBackward diodebackward_15 (.in(IC20_pin7), .out(EL));
  PullUp pullup_5 (.out(diodebackward_9_out));
  PullUp pullup_6 (.out(pullup_6_out));
  DiodeBackward diodebackward_16 (.in(IC18_pin15), .out(pullup_6_out));
  DiodeBackward diodebackward_17 (.in(IC18_pin13), .out(pullup_6_out));
  DiodeBackward diodebackward_18 (.in(IC18_pin12), .out(pullup_6_out));
  DiodeBackward diodebackward_19 (.in(IC18_pin11), .out(pullup_6_out));
  DiodeBackward diodebackward_20 (.in(IC18_pin9), .out(pullup_6_out));
  or or_1 (nPH, nJMP, nBF);
  PullUp pullup_7 (.out(EH));
  DiodeBackward diodebackward_21 (.in(IC20_pin13), .out(EH));
  DiodeBackward diodebackward_22 (.in(IC20_pin12), .out(EH));
  DiodeBackward diodebackward_23 (.in(IC20_pin7), .out(EH));
  PullUp pullup_8 (.out(pullup_8_out));
  DiodeBackward diodebackward_24 (.in(IC18_pin13), .out(pullup_8_out));
  DiodeBackward diodebackward_25 (.in(IC18_pin12), .out(pullup_8_out));
  DiodeBackward diodebackward_26 (.in(IC18_pin10), .out(pullup_8_out));
  DiodeBackward diodebackward_27 (.in(IC18_pin10), .out(diodebackward_27_out));
  DiodeBackward diodebackward_28 (.in(IC18_pin9), .out(diodebackward_27_out));
  PullUp pullup_9 (.out(diodebackward_27_out));
  DiodeBackward diodebackward_29 (.in(not_1_out), .out(nPL));
  DiodeBackward diodebackward_30 (.in(nPH), .out(nPL));
  PullUp pullup_10 (.out(nPL));
  not not_2 (IX, IC20_pin7);
  not not_3 (not_3_out, IC18_pin9);
  or or_2 (nOL, diodebackward_7_out, not_3_out);
  or or_3 (nLD, diodebackward_1_out, not_3_out);
  or or_4 (nWE, clk, IC18_pin9);
  _74540 IC20_2 (
    .pin1(1'b0), .pin2(diodebackward_9_out), .pin3(pullup_6_out), .pin4(pullup_8_out),
    .pin5(diodebackward_27_out), .pin6(diodebackward_5_out), .pin7(1'b0), .pin8(1'b0), .pin9(1'b0),
    .pin10(1'b0), .pin14(AL), .pin15(AR0), .pin16(AR1), .pin17(AR2), .pin18(AR3), .pin19(1'b0), .pin20(1'b1));  // open: pin11, pin12, pin13
  _74153 IC26_2 (
    .pin1(1'b0), .pin2(BUS7), .pin3(AR3), .pin4(AR2), .pin5(AR1), .pin6(AR0), .pin7(IC26_2_pin7),
    .pin8(1'b0), .pin9(IC26_2_pin9), .pin10(1'b0), .pin11(1'b1), .pin12(1'b0), .pin13(1'b1), .pin14(AC7),
    .pin15(AL), .pin16(1'b1));
  _74153 IC25_2 (
    .pin1(1'b0), .pin2(BUS6), .pin3(AR3), .pin4(AR2), .pin5(AR1), .pin6(AR0), .pin7(IC25_2_pin7),
    .pin8(1'b0), .pin9(IC25_2_pin9), .pin10(1'b0), .pin11(1'b1), .pin12(1'b0), .pin13(1'b1), .pin14(AC6),
    .pin15(AL), .pin16(1'b1));
  _74153 IC24_2 (
    .pin1(1'b0), .pin2(BUS5), .pin3(AR3), .pin4(AR2), .pin5(AR1), .pin6(AR0), .pin7(IC24_2_pin7),
    .pin8(1'b0), .pin9(IC24_2_pin9), .pin10(1'b0), .pin11(1'b1), .pin12(1'b0), .pin13(1'b1), .pin14(AC5),
    .pin15(AL), .pin16(1'b1));
  _74153 IC23_2 (
    .pin1(1'b0), .pin2(BUS4), .pin3(AR3), .pin4(AR2), .pin5(AR1), .pin6(AR0), .pin7(IC23_2_pin7),
    .pin8(1'b0), .pin9(IC23_2_pin9), .pin10(1'b0), .pin11(1'b1), .pin12(1'b0), .pin13(1'b1), .pin14(AC4),
    .pin15(AL), .pin16(1'b1));
  _74153 IC10 (
    .pin1(1'b0), .pin2(BUS3), .pin3(AR3), .pin4(AR2), .pin5(AR1), .pin6(AR0), .pin7(IC10_pin7), .pin8(1'b0),
    .pin9(IC10_pin9), .pin10(1'b0), .pin11(1'b1), .pin12(1'b0), .pin13(1'b1), .pin14(AC3), .pin15(AL),
    .pin16(1'b1));
  _74153 IC9 (
    .pin1(1'b0), .pin2(BUS2), .pin3(AR3), .pin4(AR2), .pin5(AR1), .pin6(AR0), .pin7(IC9_pin7), .pin8(1'b0),
    .pin9(IC9_pin9), .pin10(1'b0), .pin11(1'b1), .pin12(1'b0), .pin13(1'b1), .pin14(AC2), .pin15(AL),
    .pin16(1'b1));
  _74153 IC8 (
    .pin1(1'b0), .pin2(BUS1), .pin3(AR3), .pin4(AR2), .pin5(AR1), .pin6(AR0), .pin7(IC8_pin7), .pin8(1'b0),
    .pin9(IC8_pin9), .pin10(1'b0), .pin11(1'b1), .pin12(1'b0), .pin13(1'b1), .pin14(AC1), .pin15(AL),
    .pin16(1'b1));
  _74153 IC7 (
    .pin1(1'b0), .pin2(BUS0), .pin3(AR3), .pin4(AR2), .pin5(AR1), .pin6(AR0), .pin7(IC7_pin7), .pin8(1'b0),
    .pin9(IC7_pin9), .pin10(1'b0), .pin11(1'b1), .pin12(1'b0), .pin13(1'b1), .pin14(AC0), .pin15(AL),
    .pin16(1'b1));
  _74283 IC12 (
    .pin1(ALU5), .pin2(IC24_2_pin9), .pin3(IC24_2_pin7), .pin4(ALU4), .pin5(IC23_2_pin7), .pin6(IC23_2_pin9),
    .pin7(C1), .pin8(1'b0), .pin9(CO), .pin10(ALU7), .pin11(IC26_2_pin9), .pin12(IC26_2_pin7), .pin13(ALU6),
    .pin14(IC25_2_pin7), .pin15(IC25_2_pin9), .pin16(1'b1));
  _74283 IC11 (
    .pin1(ALU1), .pin2(IC8_pin9), .pin3(IC8_pin7), .pin4(ALU0), .pin5(IC7_pin7), .pin6(IC7_pin9), .pin7(AR0),
    .pin8(1'b0), .pin9(C1), .pin10(ALU3), .pin11(IC10_pin9), .pin12(IC10_pin7), .pin13(ALU2),
    .pin14(IC9_pin7), .pin15(IC9_pin9), .pin16(1'b1));
  LED led_9 (.in(CO));
  LED led_10 (.in(C1));
  Seven_Seg_Hex seven_seg_hex_10 (.d({AC7, AC6, AC5, AC4}), .dp(1'b0));
  _74173 IC12A (
    .pin1(in_26), .pin2(in_26), .pin3(AC4), .pin4(AC5), .pin5(AC6), .pin6(AC7), .pin7(CALC_2), .pin8(1'b0),
    .pin9(nLD), .pin10(nLD), .pin11(ALU7), .pin12(ALU6), .pin13(ALU5), .pin14(ALU4), .pin15(CLR_4),
    .pin16(1'b1));
  LED led_11 (.in(ALU7));
  LED led_12 (.in(ALU6));
  Seven_Seg_Hex seven_seg_hex_11 (.d({AC3, AC2, AC1, AC0}), .dp(1'b0));
  _74173 IC12A_2 (
    .pin1(in_3), .pin2(in_3), .pin3(AC0), .pin4(AC1), .pin5(AC2), .pin6(AC3), .pin7(CALC), .pin8(1'b0),
    .pin9(nLD), .pin10(nLD), .pin11(ALU3), .pin12(ALU2), .pin13(ALU1), .pin14(ALU0), .pin15(CLR), .pin16(1'b1));
  LED led_13 (.in(ALU3));
  LED led_14 (.in(ALU2));
  LED led_15 (.in(ALU5));
  LED led_16 (.in(ALU4));
  LED led_17 (.in(ALU1));
  LED led_18 (.in(ALU0));
  LED ZERO (.in(_7425_1_pin6));
  LED ZERO_2 (.in(_7425_2_pin6));
  _74194 IC12S (
    .pin1(1'b1), .pin2(in_27), .pin3(ALU4), .pin4(ALU5), .pin5(ALU6), .pin6(ALU7), .pin7(in_28), .pin8(1'b0),
    .pin9(SHL_2), .pin10(SHR_2), .pin11(CALC_2), .pin12(IC12S_pin15[3]), .pin13(IC12S_pin15[2]),
    .pin14(IC12S_pin15[1]), .pin15(IC12S_pin15[0]), .pin16(1'b1));
  _74194 IC12S_2 (
    .pin1(1'b1), .pin2(in_4), .pin3(ALU0), .pin4(ALU1), .pin5(ALU2), .pin6(ALU3), .pin7(in_5), .pin8(1'b0),
    .pin9(SHL), .pin10(SHR), .pin11(CALC), .pin12(IC12S_2_pin15[3]), .pin13(IC12S_2_pin15[2]),
    .pin14(IC12S_2_pin15[1]), .pin15(IC12S_2_pin15[0]), .pin16(1'b1));
  _7425 _7425_1 (
    .pin1(IC12S_pin15[0]), .pin2(IC12S_pin15[1]), .pin4(IC12S_pin15[2]), .pin5(IC12S_pin15[3]),
    .pin6(_7425_1_pin6), .pin7(1'b0), .pin9(1'b1), .pin10(1'b1), .pin12(1'b1), .pin13(1'b1), .pin14(1'b1));  // open: pin3, pin8, pin11
  _7425 _7425_2 (
    .pin1(IC12S_2_pin15[0]), .pin2(IC12S_2_pin15[1]), .pin4(IC12S_2_pin15[2]), .pin5(IC12S_2_pin15[3]),
    .pin6(_7425_2_pin6), .pin7(1'b0), .pin9(1'b1), .pin10(1'b1), .pin12(1'b1), .pin13(1'b1), .pin14(1'b1));  // open: pin3, pin8, pin11
  Seven_Seg_Hex seven_seg_hex_12 (.d(IC12S_pin15), .dp(1'b0));
  Seven_Seg_Hex seven_seg_hex_13 (.d(IC12S_2_pin15), .dp(1'b0));

  // Other names for the same wires on the sheet: CLK1 = clk

  // Notes on the sheet:
  //   clk: Hz: 2
  //   FRONT PANEL & MEMORY
  //   ADDRESS
  //   DATA
  //   CONTROL UNIT
  //   16-bit Jump Detector
  //   LOAD
  //   AND
  //   OR
  //   XOR
  //   ADD
  //   SUB
  //   STORE
  //   JMP
  //   ~W
  //   INST 8
  //   INST 9
  //   INST A
  //   INST B
  //   INST C
  //   INST D
  //   INST E
  //   INST F
  //   ALU-H
  //   ALU-L
  //   MUX3
  //   MUX2
  //   MUX1
  //   MUX0
  //   ACCUMULATOR
  //   ADDER
  //   Cout
  //   RESULT
endmodule
