// Digital circuit Building_Block_2_8_bit_Counter.dig as structural Verilog
module Building_Block_2_8_bit_Counter (
  input  HOLD_LD,
  input  CLR,
  input  nOE,
  input  LOAD,
  input  INC,
  input  BUS7,
  input  BUS6,
  input  BUS5,
  input  BUS4,
  input  BUS3,
  input  BUS2,
  input  BUS1,
  input  BUS0,
  input  CK
);

  wire IC15_pin7;
  wire [3:0] IC12_pin4, IC13_pin4, IC14_pin14, IC15_pin14;

  _74173 IC13 (
    .pin1(nOE), .pin2(nOE), .pin3(IC13_pin4[0]), .pin4(IC13_pin4[1]), .pin5(IC13_pin4[2]),
    .pin6(IC13_pin4[3]), .pin7(CK), .pin8(1'b0), .pin9(HOLD_LD), .pin10(HOLD_LD), .pin11(BUS7), .pin12(BUS6),
    .pin13(BUS5), .pin14(BUS4), .pin15(CLR), .pin16(1'b1));
  _74173 IC12 (
    .pin1(nOE), .pin2(nOE), .pin3(IC12_pin4[0]), .pin4(IC12_pin4[1]), .pin5(IC12_pin4[2]),
    .pin6(IC12_pin4[3]), .pin7(CK), .pin8(1'b0), .pin9(HOLD_LD), .pin10(HOLD_LD), .pin11(BUS3), .pin12(BUS2),
    .pin13(BUS1), .pin14(BUS0), .pin15(CLR), .pin16(1'b1));
  Seven_Seg_Hex seven_seg_hex_1 (.d(IC13_pin4), .dp(1'b0));
  Seven_Seg_Hex seven_seg_hex_2 (.d(IC12_pin4), .dp(1'b0));
  _74163 IC15 (
    .pin1(1'b1), .pin2(INC), .pin3(IC13_pin4[0]), .pin4(IC13_pin4[1]), .pin5(IC13_pin4[2]),
    .pin6(IC13_pin4[3]), .pin7(IC15_pin7), .pin8(1'b0), .pin9(LOAD), .pin10(1'b1), .pin11(IC15_pin14[3]),
    .pin12(IC15_pin14[2]), .pin13(IC15_pin14[1]), .pin14(IC15_pin14[0]), .pin16(1'b1));  // open: pin15
  _74163 IC14 (
    .pin1(1'b1), .pin2(INC), .pin3(IC12_pin4[0]), .pin4(IC12_pin4[1]), .pin5(IC12_pin4[2]),
    .pin6(IC12_pin4[3]), .pin7(1'b1), .pin8(1'b0), .pin9(LOAD), .pin10(1'b1), .pin11(IC14_pin14[3]),
    .pin12(IC14_pin14[2]), .pin13(IC14_pin14[1]), .pin14(IC14_pin14[0]), .pin15(IC15_pin7), .pin16(1'b1));
  Seven_Seg_Hex seven_seg_hex_3 (.d(IC15_pin14), .dp(1'b0));
  Seven_Seg_Hex seven_seg_hex_4 (.d(IC14_pin14), .dp(1'b0));

  // Notes on the sheet:
  //   8-bit Counter
endmodule
