// Digital circuit Building_Block_3_ALU.dig as structural Verilog
module Building_Block_3_ALU (
  input  Cin,
  input  AL,
  input  AR3,
  input  AR2,
  input  AR1,
  input  AR0,
  input  AC3,
  input  AC2,
  input  AC1,
  input  AC0,
  input  BUS3,
  input  BUS2,
  input  BUS1,
  input  BUS0,
  output B0,
  output B1,
  output A1,
  output A2,
  output B2,
  output B3,
  output A3,
  output A0,
  output OUT3,
  output OUT2,
  output OUT1,
  output OUT0,
  output COUT
);

  _74153 IC10 (
    .pin1(1'b0), .pin2(BUS3), .pin3(AR3), .pin4(AR2), .pin5(AR1), .pin6(AR0), .pin7(A3), .pin8(1'b0),
    .pin9(B3), .pin10(1'b0), .pin11(1'b1), .pin12(1'b0), .pin13(1'b1), .pin14(AC3), .pin15(AL), .pin16(1'b1));
  _74153 IC9 (
    .pin1(1'b0), .pin2(BUS2), .pin3(AR3), .pin4(AR2), .pin5(AR1), .pin6(AR0), .pin7(A2), .pin8(1'b0),
    .pin9(B2), .pin10(1'b0), .pin11(1'b1), .pin12(1'b0), .pin13(1'b1), .pin14(AC2), .pin15(AL), .pin16(1'b1));
  _74153 IC8 (
    .pin1(1'b0), .pin2(BUS1), .pin3(AR3), .pin4(AR2), .pin5(AR1), .pin6(AR0), .pin7(A1), .pin8(1'b0),
    .pin9(B1), .pin10(1'b0), .pin11(1'b1), .pin12(1'b0), .pin13(1'b1), .pin14(AC1), .pin15(AL), .pin16(1'b1));
  _74153 IC7 (
    .pin1(1'b0), .pin2(BUS0), .pin3(AR3), .pin4(AR2), .pin5(AR1), .pin6(AR0), .pin7(A0), .pin8(1'b0),
    .pin9(B0), .pin10(1'b0), .pin11(1'b1), .pin12(1'b0), .pin13(1'b1), .pin14(AC0), .pin15(AL), .pin16(1'b1));
  _74283 IC11 (
    .pin1(OUT1), .pin2(B1), .pin3(A1), .pin4(OUT0), .pin5(A0), .pin6(B0), .pin7(Cin), .pin8(1'b0),
    .pin9(COUT), .pin10(OUT3), .pin11(B3), .pin12(A3), .pin13(OUT2), .pin14(A2), .pin15(B2), .pin16(1'b1));
  LED led_1 (.in(COUT));
  LED led_2 (.in(OUT3));
  LED led_3 (.in(OUT2));
  LED led_4 (.in(OUT1));
  LED led_5 (.in(OUT0));

  // Notes on the sheet:
  //   4-bit ALU
  //   ADD  1100
  //   SUB  0011 plus Cin
  //   AND  1000 plus AL
  //   OR      1110 plus AL
  //   XOR   0110 plus AL
  //   0000 = 0x0 // Q=0x00  
  //   1111 = 0xf // Q=0xff  
  //   1010 = 0xa // Q=A     
  //   1100 = 0xc // Q=B     
  //   0101 = 0x5 // Q=/A    
  //   0011 = 0x3 // Q=/B    
  //   1110 = 0xe // Q= A| B 
  //   1101 = 0xd // Q=/A| B 
  //   1011 = 0xb // Q= A|/B 
  //   0111 = 0x7 // Q=/A|/B 
  //   1000 = 0x8 // Q= A& B 
  //   0100 = 0x4 // Q=/A& B 
  //   0010 = 0x2 // Q= A&/B 
  //   0001 = 0x1 // Q=/A&/B 
  //   0110 = 0x6 // Q=  A XOR B 
  //   1001 = 0x9 // Q=/(A XOR B)
  //   MUX3
  //   MUX2
  //   MUX1
  //   MUX0
  //   ADDER
  //   Cout
  //   RESULT
endmodule
