// Digital circuit Building_Block_4_Instruction_Decoder.dig as structural Verilog
module Building_Block_4_Instruction_Decoder (
  input  in_1,
  input  in_2,
  input  in_3,
  input  in_4
);

  wire diodebackward_3_out, diodebackward_11_out, IC18_pin7, IC18_pin9, IC18_pin10, IC18_pin11, IC18_pin12,
       IC18_pin13, IC18_pin14, IC18_pin15, IC19_pin7, IC19_pin9, IC19_pin10, IC19_pin11, IC19_pin12,
       IC19_pin13, IC19_pin14, IC19_pin15, IC20_pin11, IC20_pin12, IC20_pin13, IC20_pin14, IC20_pin15,
       IC20_pin16, IC20_pin17, IC20_pin18, pullup_1_out, pullup_2_out, pullup_5_out;

  _74138 IC18 (
    .pin1(in_1), .pin2(in_2), .pin3(in_3), .pin4(in_4), .pin5(1'b0), .pin6(1'b1), .pin7(IC18_pin7),
    .pin8(1'b0), .pin9(IC18_pin9), .pin10(IC18_pin10), .pin11(IC18_pin11), .pin12(IC18_pin12),
    .pin13(IC18_pin13), .pin14(IC18_pin14), .pin15(IC18_pin15), .pin16(1'b1));
  _74138 IC19 (
    .pin1(in_1), .pin2(in_2), .pin3(in_3), .pin4(1'b0), .pin5(1'b0), .pin6(in_4), .pin7(IC19_pin7),
    .pin8(1'b0), .pin9(IC19_pin9), .pin10(IC19_pin10), .pin11(IC19_pin11), .pin12(IC19_pin12),
    .pin13(IC19_pin13), .pin14(IC19_pin14), .pin15(IC19_pin15), .pin16(1'b1));
  PullUp pullup_1 (.out(pullup_1_out));
  DiodeBackward diodebackward_1 (.in(IC19_pin15), .out(pullup_1_out));
  PullUp pullup_2 (.out(pullup_2_out));
  DiodeBackward diodebackward_2 (.in(IC18_pin15), .out(pullup_2_out));
  DiodeBackward diodebackward_3 (.in(IC18_pin15), .out(diodebackward_3_out));
  DiodeBackward diodebackward_4 (.in(IC18_pin14), .out(pullup_2_out));
  DiodeBackward diodebackward_5 (.in(IC18_pin13), .out(pullup_2_out));
  DiodeBackward diodebackward_6 (.in(IC18_pin13), .out(diodebackward_3_out));
  DiodeBackward diodebackward_7 (.in(IC18_pin12), .out(diodebackward_3_out));
  DiodeBackward diodebackward_8 (.in(IC18_pin11), .out(pullup_2_out));
  DiodeBackward diodebackward_9 (.in(IC18_pin11), .out(diodebackward_3_out));
  DiodeBackward diodebackward_10 (.in(IC18_pin9), .out(diodebackward_3_out));
  PullUp pullup_3 (.out(diodebackward_3_out));
  DiodeBackward diodebackward_11 (.in(IC18_pin13), .out(diodebackward_11_out));
  DiodeBackward diodebackward_12 (.in(IC18_pin12), .out(diodebackward_11_out));
  DiodeBackward diodebackward_13 (.in(IC18_pin10), .out(diodebackward_11_out));
  PullUp pullup_4 (.out(diodebackward_11_out));
  PullUp pullup_5 (.out(pullup_5_out));
  DiodeBackward diodebackward_14 (.in(IC18_pin10), .out(pullup_5_out));
  DiodeBackward diodebackward_15 (.in(IC18_pin9), .out(pullup_5_out));
  _74540 IC20 (
    .pin1(1'b0), .pin2(1'b0), .pin3(1'b0), .pin4(1'b0), .pin5(pullup_5_out), .pin6(diodebackward_11_out),
    .pin7(diodebackward_3_out), .pin8(pullup_2_out), .pin9(pullup_1_out), .pin10(1'b0), .pin11(IC20_pin11),
    .pin12(IC20_pin12), .pin13(IC20_pin13), .pin14(IC20_pin14), .pin15(IC20_pin15), .pin16(IC20_pin16),
    .pin17(IC20_pin17), .pin18(IC20_pin18), .pin19(1'b0), .pin20(1'b1));

  // Notes on the sheet:
  //   INSTRUCTION INPUT
  //   INSTRUCTION DECODER
  //   Control signals to ALU
  //   LOAD
  //   AND
  //   OR
  //   XOR
  //   ADD
  //   SUB
  //   STORE
  //   JMP
endmodule
