// Digital circuit Compute_Module_1.dig as structural Verilog
module Compute_Module_1 (
  input  SEL_PC,
  input  SEL_DATA,
  input  CLK,
  input  in_4,
  input  in_5,
  input  in_6,
  input  in_7,
  input  in_8,
  input  in_9,
  input  D0,
  input  D1,
  input  D2,
  input  D3,
  input  D4,
  input  D5,
  input  D6,
  input  D7,
  input  D8,
  input  D9,
  input  D10,
  input  D11,
  input  D12,
  input  D13,
  input  D14,
  input  D15,
  output out_26,
  output out_27,
  output out_28,
  output out_29,
  output out_30,
  output out_31,
  output out_32,
  output out_33,
  output out_34,
  output out_35,
  output out_36,
  output out_37
);

  wire cm_1_1_p18, cm_1_1_p19, cm_1_1_p20, cm_1_1_p21, cm_1_1_p22, cm_1_1_p23, cm_1_2_cout;
  wire [3:0] cm_1_2_dout0, cm_1_2_dout7, undriven, undriven_2;

  Seven_Seg_Hex seven_seg_hex_1 (.d({out_26, out_27, out_28, out_29}), .dp(1'b0));
  Seven_Seg_Hex seven_seg_hex_2 (.d({D15, D14, D13, D12}), .dp(1'b0));
  Seven_Seg_Hex seven_seg_hex_3 (.d(cm_1_2_dout7), .dp(1'b0));
  Seven_Seg_Hex seven_seg_hex_4 (.d({out_30, out_31, out_32, out_33}), .dp(1'b0));
  Seven_Seg_Hex seven_seg_hex_5 (.d({D11, D10, D9, D8}), .dp(1'b0));
  Seven_Seg_Hex seven_seg_hex_6 (.d(cm_1_2_dout0), .dp(1'b0));
  Seven_Seg_Hex seven_seg_hex_7 (.d({out_34, out_35, out_36, out_37}), .dp(1'b0));
  Seven_Seg_Hex seven_seg_hex_8 (.d({D7, D6, D5, D4}), .dp(1'b0));
  Seven_Seg_Hex seven_seg_hex_9 (.d(undriven), .dp(1'b0));
  Seven_Seg_Hex seven_seg_hex_10 (.d({D3, D2, D1, D0}), .dp(1'b0));
  Seven_Seg_Hex seven_seg_hex_11 (.d(undriven_2), .dp(1'b0));
  // CM_1 cm_1_1: pin names not known; wires that end beside it: CLK, in_4, in_5, in_6, in_7, in_8, D0, D1, D2, D3, D4, D5, D6, D7, undriven_2[0], undriven_2[1], 1'b1, cm_1_1_p18, cm_1_1_p19, cm_1_1_p20, cm_1_1_p21, cm_1_1_p22, cm_1_1_p23, SEL_PC, SEL_DATA, in_9
  CM_1 cm_1_2 (
    .Din0(D8), .Cin(cm_1_1_p22), .Dout0(cm_1_2_dout0[0]), .Dout1(cm_1_2_dout0[1]), .Dout2(cm_1_2_dout0[2]),
    .Dout3(cm_1_2_dout0[3]), .Din2(D10), .Din3(D11), .Din4(D12), .Dout4(cm_1_2_dout7[0]),
    .Dout5(cm_1_2_dout7[1]), .Dout6(cm_1_2_dout7[2]), .Dout7(cm_1_2_dout7[3]), .Din5(D13), .Din6(D14),
    .Din7(D15), .A3(out_28), .A2(out_29), .A1(out_30), .PCin(cm_1_1_p23), .A0(out_31), .Sel_Data(SEL_DATA),
    .Sel_PC(SEL_PC), .A5(out_26), .A4(out_27), .IR2(cm_1_1_p19), .IR3(cm_1_1_p18), .IR0(cm_1_1_p21),
    .IR1(cm_1_1_p20), .Din1(D9), .Cout(cm_1_2_cout), .VCC(1'b1), .GND(1'b0), .PCout(cm_1_2_cout), .VSS(1'b0),
    .CLK(CLK));  // open: I3, I2, I1, I0

  // Other names for the same wires on the sheet: A0 = out_26; A1 = out_27; A2 = out_28; A3 = out_29; A4 = out_30;
  //   A5 = out_31; A6 = out_32; A7 = out_33; A8 = out_34; A9 = out_35; A10 = out_36; A11 = out_37

  // Notes on the sheet:
  //   ADDRESS
  //   DATA IN
  //   DATA OUT
endmodule
