// Digital circuit Lesson_1_LEDS_Switches.dig as structural Verilog
module Lesson_1_LEDS_Switches (
  input  HOLD_LD,
  input  CLR,
  input  CK,
  input  nOE
);

  wire IC1_pin2, IC1_pin3, IC1_pin8, IC1_pin11, IC2_pin2, IC2_pin3, IC2_pin8, IC2_pin11, IC3_pin2, IC3_pin3,
       IC3_pin8, IC3_pin11, IC4_pin1, IC4_pin2, IC4_pin3, IC4_pin8, IC4_pin11;
  wire [3:0] IC2_pin5, IC3_pin5, IC5_pin3, IC6_pin6;

  _7474 IC4 (
    .pin1(IC4_pin1), .pin2(IC4_pin2), .pin3(IC4_pin3), .pin4(1'b1), .pin5(IC3_pin5[3]), .pin6(IC4_pin2),
    .pin7(1'b0), .pin8(IC4_pin8), .pin9(IC3_pin5[2]), .pin10(1'b1), .pin11(IC4_pin11), .pin12(IC4_pin8),
    .pin13(IC4_pin1), .pin14(1'b1));
  _7474 IC3 (
    .pin1(IC4_pin1), .pin2(IC3_pin2), .pin3(IC3_pin3), .pin4(1'b1), .pin5(IC3_pin5[0]), .pin6(IC3_pin2),
    .pin7(1'b0), .pin8(IC3_pin8), .pin9(IC3_pin5[1]), .pin10(1'b1), .pin11(IC3_pin11), .pin12(IC3_pin8),
    .pin13(IC4_pin1), .pin14(1'b1));
  LED led_1 (.in(IC3_pin5[3]));
  Button button_1 (.out(IC4_pin3));
  LED led_2 (.in(IC3_pin5[2]));
  Button button_2 (.out(IC4_pin11));
  LED led_3 (.in(IC3_pin5[1]));
  Button button_3 (.out(IC3_pin11));
  LED led_4 (.in(IC3_pin5[0]));
  Button button_4 (.out(IC3_pin3));
  _7474 IC2 (
    .pin1(IC4_pin1), .pin2(IC2_pin2), .pin3(IC2_pin3), .pin4(1'b1), .pin5(IC2_pin5[3]), .pin6(IC2_pin2),
    .pin7(1'b0), .pin8(IC2_pin8), .pin9(IC2_pin5[2]), .pin10(1'b1), .pin11(IC2_pin11), .pin12(IC2_pin8),
    .pin13(IC4_pin1), .pin14(1'b1));
  LED led_5 (.in(IC2_pin5[3]));
  Button button_5 (.out(IC2_pin3));
  LED led_6 (.in(IC2_pin5[2]));
  Button button_6 (.out(IC2_pin11));
  LED led_7 (.in(IC2_pin5[1]));
  _7474 IC1 (
    .pin1(IC4_pin1), .pin2(IC1_pin2), .pin3(IC1_pin3), .pin4(1'b1), .pin5(IC2_pin5[0]), .pin6(IC1_pin2),
    .pin7(1'b0), .pin8(IC1_pin8), .pin9(IC2_pin5[1]), .pin10(1'b1), .pin11(IC1_pin11), .pin12(IC1_pin8),
    .pin13(IC4_pin1), .pin14(1'b1));
  Button button_7 (.out(IC1_pin11));
  LED led_8 (.in(IC2_pin5[0]));
  Button button_8 (.out(IC1_pin3));
  Seven_Seg_Hex seven_seg_hex_1 (.d(IC3_pin5), .dp(1'b0));
  Seven_Seg_Hex seven_seg_hex_2 (.d(IC2_pin5), .dp(1'b0));
  Button #(.activeLow("true")) CLEAR (.out(IC4_pin1));
  _74173 IC6 (
    .pin1(nOE), .pin2(nOE), .pin3(IC6_pin6[0]), .pin4(IC6_pin6[1]), .pin5(IC6_pin6[2]), .pin6(IC6_pin6[3]),
    .pin7(CK), .pin8(1'b0), .pin9(HOLD_LD), .pin10(HOLD_LD), .pin11(IC3_pin5[3]), .pin12(IC3_pin5[2]),
    .pin13(IC3_pin5[1]), .pin14(IC3_pin5[0]), .pin15(CLR), .pin16(1'b1));
  _74173 IC5 (
    .pin1(nOE), .pin2(nOE), .pin3(IC5_pin3[0]), .pin4(IC5_pin3[1]), .pin5(IC5_pin3[2]), .pin6(IC5_pin3[3]),
    .pin7(CK), .pin8(1'b0), .pin9(HOLD_LD), .pin10(HOLD_LD), .pin11(IC2_pin5[3]), .pin12(IC2_pin5[2]),
    .pin13(IC2_pin5[1]), .pin14(IC2_pin5[0]), .pin15(CLR), .pin16(1'b1));
  Seven_Seg_Hex seven_seg_hex_3 (.d(IC6_pin6), .dp(1'b0));
  Seven_Seg_Hex seven_seg_hex_4 (.d(IC5_pin3), .dp(1'b0));
endmodule
