// Digital circuit Nybble_6.dig as structural Verilog
module Nybble_6 (
  input  HOLD_LD,
  input  CLR,
  input  nOE,
  input  LOAD,
  input  INC,
  input  DEP,
  input  in_7,
  input  in_8,
  input  in_9,
  input  in_10,
  input  in_11,
  input  in_12,
  input  nRD,
  input  nWR,
  input  HOLD_LD_2,
  input  CLR_2,
  input  nOE_2,
  input  CK,
  input  Cin,
  input  BUS3,
  input  BUS2,
  input  BUS1,
  input  BUS0,
  input  CALC,
  input  CLR_3,
  input  in_27,
  input  in_28,
  input  in_29,
  input  in_30,
  input  SHR,
  input  SHL,
  input  in_33,
  input  in_34,
  input  in_35,
  input  in_36,
  output COUT
);

  wire AL, AR0, AR1, AR2, AR3, button_7_out, diodebackward_2_out, diodebackward_7_out, IC1_pin2, IC1_pin3,
       IC1_pin8, IC2_pin2, IC2_pin3, IC2_pin8, IC2_pin11, IC3_pin2, IC3_pin3, IC3_pin8, IC3_pin11, IC4_pin1,
       IC4_pin2, IC4_pin3, IC4_pin8, IC4_pin11, IC7_pin7, IC7_pin9, IC8_pin7, IC8_pin9, IC9_pin7, IC9_pin9,
       IC10_pin7, IC10_pin9, IC11_pin1, IC11_pin4, IC11_pin10, IC11_pin13, IC16_pin10, IC18_pin7, IC18_pin9,
       IC18_pin10, IC18_pin11, IC18_pin12, IC18_pin13, IC18_pin14, IC18_pin15, IC19_pin7, IC19_pin9,
       IC19_pin10, IC19_pin11, IC19_pin12, IC19_pin13, IC19_pin14, IC19_pin15, IC20_pin16, IC20_pin17,
       IC20_pin18, pullup_1_out, pullup_4_out, pullup_5_out;
  wire [3:0] IC4_pin9, IC6_pin3, IC7_pin14, IC12S_pin15, IC13_pin5, IC13_pin12, IC14_pin6, IC15_pin14,
       IC16_pin14, IC17_p10;

  _7474 IC4 (
    .pin1(IC4_pin1), .pin2(IC4_pin2), .pin3(IC4_pin3), .pin4(1'b1), .pin5(IC4_pin9[3]), .pin6(IC4_pin2),
    .pin7(1'b0), .pin8(IC4_pin8), .pin9(IC4_pin9[2]), .pin10(1'b1), .pin11(IC4_pin11), .pin12(IC4_pin8),
    .pin13(IC4_pin1), .pin14(1'b1));
  Button #(.activeLow("true")) CLEAR (.out(IC4_pin1));
  _74173 IC14 (
    .pin1(nOE), .pin2(nOE), .pin3(IC14_pin6[0]), .pin4(IC14_pin6[1]), .pin5(IC14_pin6[2]),
    .pin6(IC14_pin6[3]), .pin7(DEP), .pin8(1'b0), .pin9(HOLD_LD), .pin10(HOLD_LD), .pin11(IC4_pin9[3]),
    .pin12(IC4_pin9[2]), .pin13(IC4_pin9[1]), .pin14(IC4_pin9[0]), .pin15(CLR), .pin16(1'b1));
  _74173 IC13 (
    .pin1(nOE), .pin2(nOE), .pin3(IC13_pin5[0]), .pin4(IC13_pin5[1]), .pin5(IC13_pin5[2]),
    .pin6(IC13_pin5[3]), .pin7(DEP), .pin8(1'b0), .pin9(HOLD_LD), .pin10(HOLD_LD), .pin11(IC13_pin12[3]),
    .pin12(IC13_pin12[2]), .pin13(IC13_pin12[1]), .pin14(IC13_pin12[0]), .pin15(CLR), .pin16(1'b1));
  LED led_1 (.in(IC4_pin9[3]));
  _7474 IC3 (
    .pin1(IC4_pin1), .pin2(IC3_pin2), .pin3(IC3_pin3), .pin4(1'b1), .pin5(IC4_pin9[0]), .pin6(IC3_pin2),
    .pin7(1'b0), .pin8(IC3_pin8), .pin9(IC4_pin9[1]), .pin10(1'b1), .pin11(IC3_pin11), .pin12(IC3_pin8),
    .pin13(IC4_pin1), .pin14(1'b1));
  Button button_1 (.out(IC4_pin3));
  Seven_Seg_Hex seven_seg_hex_1 (.d(IC14_pin6), .dp(1'b0));
  LED led_2 (.in(IC4_pin9[2]));
  Button button_2 (.out(IC4_pin11));
  Seven_Seg_Hex seven_seg_hex_2 (.d(IC13_pin5), .dp(1'b0));
  LED led_3 (.in(IC4_pin9[1]));
  Button button_3 (.out(IC3_pin11));
  _74163 IC16 (
    .pin1(1'b1), .pin2(DEP), .pin3(IC14_pin6[0]), .pin4(IC14_pin6[1]), .pin5(IC14_pin6[2]),
    .pin6(IC14_pin6[3]), .pin7(1'b1), .pin8(1'b0), .pin9(LOAD), .pin10(IC16_pin10), .pin11(IC16_pin14[3]),
    .pin12(IC16_pin14[2]), .pin13(IC16_pin14[1]), .pin14(IC16_pin14[0]), .pin16(1'b1));  // open: pin15
  LED led_4 (.in(IC4_pin9[0]));
  _7474 IC2 (
    .pin1(IC4_pin1), .pin2(IC2_pin2), .pin3(IC2_pin3), .pin4(1'b1), .pin5(IC13_pin12[3]), .pin6(IC2_pin2),
    .pin7(1'b0), .pin8(IC2_pin8), .pin9(IC13_pin12[2]), .pin10(1'b1), .pin11(IC2_pin11), .pin12(IC2_pin8),
    .pin13(IC4_pin1), .pin14(1'b1));
  Button button_4 (.out(IC3_pin3));
  LED led_5 (.in(IC13_pin12[3]));
  Button button_5 (.out(IC2_pin3));
  LED led_6 (.in(IC13_pin12[2]));
  Button button_6 (.out(IC2_pin11));
  Seven_Seg_Hex seven_seg_hex_3 (.d(IC16_pin14), .dp(1'b0));
  LED led_7 (.in(IC13_pin12[1]));
  Button button_7 (.out(button_7_out));
  Seven_Seg_Hex seven_seg_hex_4 (.d(IC15_pin14), .dp(1'b0));
  _7474 IC1 (
    .pin1(IC4_pin1), .pin2(IC1_pin2), .pin3(IC1_pin3), .pin4(1'b1), .pin5(IC13_pin12[0]), .pin6(IC1_pin2),
    .pin7(1'b0), .pin8(IC1_pin8), .pin9(IC13_pin12[1]), .pin10(1'b1), .pin11(button_7_out), .pin12(IC1_pin8),
    .pin13(IC4_pin1), .pin14(1'b1));
  Seven_Seg_Hex seven_seg_hex_5 (.d(IC4_pin9), .dp(1'b0));
  LED led_8 (.in(IC13_pin12[0]));
  Button button_8 (.out(IC1_pin3));
  _74163 IC15 (
    .pin1(1'b1), .pin2(DEP), .pin3(IC13_pin5[0]), .pin4(IC13_pin5[1]), .pin5(IC13_pin5[2]),
    .pin6(IC13_pin5[3]), .pin7(1'b1), .pin8(1'b0), .pin9(LOAD), .pin10(1'b1), .pin11(IC15_pin14[3]),
    .pin12(IC15_pin14[2]), .pin13(IC15_pin14[1]), .pin14(IC15_pin14[0]), .pin15(IC16_pin10), .pin16(1'b1));
  Seven_Seg_Hex seven_seg_hex_6 (.d(IC13_pin12), .dp(1'b0));
  // A623308A IC17: pin names not known; wires that end beside it: in_7, IC16_pin14[3], IC16_pin14[2], IC16_pin14[1], IC16_pin14[0], IC15_pin14[3], IC15_pin14[2], IC15_pin14[1], IC15_pin14[0], IC17_p10[0], IC17_p10[1], IC17_p10[2], 1'b0, 1'b1, nWR, in_8, in_9, in_10, nRD, in_11, in_12, IC6_pin3[3]
  _74173 IC6 (
    .pin1(nOE_2), .pin2(nOE_2), .pin3(IC6_pin3[0]), .pin4(IC6_pin3[1]), .pin5(IC6_pin3[2]),
    .pin6(IC6_pin3[3]), .pin7(CK), .pin8(1'b0), .pin9(HOLD_LD_2), .pin10(HOLD_LD_2), .pin11(IC4_pin9[3]),
    .pin12(IC4_pin9[2]), .pin13(IC4_pin9[1]), .pin14(IC4_pin9[0]), .pin15(CLR_2), .pin16(1'b1));
  _74173 IC5 (
    .pin1(nOE_2), .pin2(nOE_2), .pin3(IC17_p10[0]), .pin4(IC17_p10[1]), .pin5(IC17_p10[2]),
    .pin6(IC17_p10[3]), .pin7(CK), .pin8(1'b0), .pin9(HOLD_LD_2), .pin10(HOLD_LD_2), .pin11(IC13_pin12[3]),
    .pin12(IC13_pin12[2]), .pin13(IC13_pin12[1]), .pin14(IC13_pin12[0]), .pin15(CLR_2), .pin16(1'b1));
  Seven_Seg_Hex seven_seg_hex_7 (.d(IC6_pin3), .dp(1'b0));
  Seven_Seg_Hex seven_seg_hex_8 (.d(IC17_p10), .dp(1'b0));
  _74153 IC10 (
    .pin1(1'b0), .pin2(BUS3), .pin3(AR3), .pin4(AR2), .pin5(AR1), .pin6(AR0), .pin7(IC10_pin7), .pin8(1'b0),
    .pin9(IC10_pin9), .pin10(1'b0), .pin11(1'b1), .pin12(1'b0), .pin13(1'b1), .pin14(IC7_pin14[3]),
    .pin15(AL), .pin16(1'b1));
  _74153 IC9 (
    .pin1(1'b0), .pin2(BUS2), .pin3(AR3), .pin4(AR2), .pin5(AR1), .pin6(AR0), .pin7(IC9_pin7), .pin8(1'b0),
    .pin9(IC9_pin9), .pin10(1'b0), .pin11(1'b1), .pin12(1'b0), .pin13(1'b1), .pin14(IC7_pin14[2]),
    .pin15(AL), .pin16(1'b1));
  _74153 IC8 (
    .pin1(1'b0), .pin2(BUS1), .pin3(AR3), .pin4(AR2), .pin5(AR1), .pin6(AR0), .pin7(IC8_pin7), .pin8(1'b0),
    .pin9(IC8_pin9), .pin10(1'b0), .pin11(1'b1), .pin12(1'b0), .pin13(1'b1), .pin14(IC7_pin14[1]),
    .pin15(AL), .pin16(1'b1));
  _74153 IC7 (
    .pin1(1'b0), .pin2(BUS0), .pin3(AR3), .pin4(AR2), .pin5(AR1), .pin6(AR0), .pin7(IC7_pin7), .pin8(1'b0),
    .pin9(IC7_pin9), .pin10(1'b0), .pin11(1'b1), .pin12(1'b0), .pin13(1'b1), .pin14(IC7_pin14[0]),
    .pin15(AL), .pin16(1'b1));
  _74283 IC11 (
    .pin1(IC11_pin1), .pin2(IC8_pin9), .pin3(IC8_pin7), .pin4(IC11_pin4), .pin5(IC7_pin7), .pin6(IC7_pin9),
    .pin7(AR0), .pin8(1'b0), .pin9(COUT), .pin10(IC11_pin10), .pin11(IC10_pin9), .pin12(IC10_pin7),
    .pin13(IC11_pin13), .pin14(IC9_pin7), .pin15(IC9_pin9), .pin16(1'b1));
  LED led_9 (.in(COUT));
  Seven_Seg_Hex seven_seg_hex_9 (.d(IC7_pin14), .dp(1'b0));
  LED led_10 (.in(IC11_pin10));
  _74173 IC12A (
    .pin1(in_28), .pin2(in_28), .pin3(IC7_pin14[0]), .pin4(IC7_pin14[1]), .pin5(IC7_pin14[2]),
    .pin6(IC7_pin14[3]), .pin7(CALC), .pin8(1'b0), .pin9(in_27), .pin10(in_27), .pin11(IC11_pin10),
    .pin12(IC11_pin13), .pin13(IC11_pin1), .pin14(IC11_pin4), .pin15(CLR_3), .pin16(1'b1));
  LED led_11 (.in(IC11_pin13));
  LED led_12 (.in(IC11_pin1));
  LED led_13 (.in(IC11_pin4));
  _74194 IC12S (
    .pin1(1'b1), .pin2(in_29), .pin3(IC11_pin4), .pin4(IC11_pin1), .pin5(IC11_pin13), .pin6(IC11_pin10),
    .pin7(in_30), .pin8(1'b0), .pin9(SHL), .pin10(SHR), .pin11(CALC), .pin12(IC12S_pin15[3]),
    .pin13(IC12S_pin15[2]), .pin14(IC12S_pin15[1]), .pin15(IC12S_pin15[0]), .pin16(1'b1));
  Seven_Seg_Hex seven_seg_hex_10 (.d(IC12S_pin15), .dp(1'b0));
  _74138 IC18 (
    .pin1(in_33), .pin2(in_34), .pin3(in_35), .pin4(in_36), .pin5(1'b0), .pin6(1'b1), .pin7(IC18_pin7),
    .pin8(1'b0), .pin9(IC18_pin9), .pin10(IC18_pin10), .pin11(IC18_pin11), .pin12(IC18_pin12),
    .pin13(IC18_pin13), .pin14(IC18_pin14), .pin15(IC18_pin15), .pin16(1'b1));
  _74138 IC19 (
    .pin1(in_33), .pin2(in_34), .pin3(in_35), .pin4(1'b0), .pin5(1'b0), .pin6(in_36), .pin7(IC19_pin7),
    .pin8(1'b0), .pin9(IC19_pin9), .pin10(IC19_pin10), .pin11(IC19_pin11), .pin12(IC19_pin12),
    .pin13(IC19_pin13), .pin14(IC19_pin14), .pin15(IC19_pin15), .pin16(1'b1));
  PullUp pullup_1 (.out(pullup_1_out));
  DiodeBackward diodebackward_1 (.in(in_35), .out(pullup_1_out));
  DiodeBackward diodebackward_2 (.in(IC18_pin15), .out(diodebackward_2_out));
  DiodeBackward diodebackward_3 (.in(IC18_pin14), .out(diodebackward_2_out));
  DiodeBackward diodebackward_4 (.in(IC18_pin13), .out(diodebackward_2_out));
  DiodeBackward diodebackward_5 (.in(IC18_pin11), .out(diodebackward_2_out));
  DiodeBackward diodebackward_6 (.in(IC18_pin7), .out(pullup_1_out));
  PullUp pullup_2 (.out(diodebackward_2_out));
  DiodeBackward diodebackward_7 (.in(IC18_pin15), .out(diodebackward_7_out));
  DiodeBackward diodebackward_8 (.in(IC18_pin13), .out(diodebackward_7_out));
  DiodeBackward diodebackward_9 (.in(IC18_pin12), .out(diodebackward_7_out));
  DiodeBackward diodebackward_10 (.in(IC18_pin11), .out(diodebackward_7_out));
  DiodeBackward diodebackward_11 (.in(IC18_pin9), .out(diodebackward_7_out));
  PullUp pullup_3 (.out(diodebackward_7_out));
  PullUp pullup_4 (.out(pullup_4_out));
  DiodeBackward diodebackward_12 (.in(IC18_pin13), .out(pullup_4_out));
  DiodeBackward diodebackward_13 (.in(IC18_pin12), .out(pullup_4_out));
  DiodeBackward diodebackward_14 (.in(IC18_pin10), .out(pullup_4_out));
  PullUp pullup_5 (.out(pullup_5_out));
  DiodeBackward diodebackward_15 (.in(IC18_pin10), .out(pullup_5_out));
  DiodeBackward diodebackward_16 (.in(IC18_pin9), .out(pullup_5_out));
  _74540 IC20 (
    .pin1(1'b0), .pin2(1'b0), .pin3(1'b0), .pin4(1'b0), .pin5(pullup_5_out), .pin6(pullup_4_out),
    .pin7(diodebackward_7_out), .pin8(diodebackward_2_out), .pin9(pullup_1_out), .pin10(1'b0), .pin11(AL),
    .pin12(AR3), .pin13(AR2), .pin14(AR1), .pin15(AR0), .pin16(IC20_pin16), .pin17(IC20_pin17),
    .pin18(IC20_pin18), .pin19(1'b0), .pin20(1'b1));

  // Notes on the sheet:
  //   Front Panel Interface
  //   ADDRESS
  //   DATA
  //   MUX3
  //   MUX2
  //   MUX1
  //   MUX0
  //   ACCUMULATOR
  //   ADDER
  //   Cout
  //   RESULT
  //   INSTRUCTION DECODER
  //   LOAD
  //   AND
  //   XOR
  //   ADD
  //   SUB
  //   STORE
  //   JMP
  //   OR
endmodule
