// Digital circuit small_front_panel_1.dig as structural Verilog
module small_front_panel_1 (
  input  HOLD_LD,
  input  CLR,
  input  nOE,
  input  LOAD,
  input  INC,
  input  DEP,
  input  in_7,
  input  in_8,
  input  in_9,
  input  in_10,
  input  in_11,
  input  in_12,
  input  nRD,
  input  nWR,
  input  HOLD_LD_2,
  input  CLR_2,
  input  nOE_2,
  input  CK
);

  wire button_7_out, IC1_pin2, IC1_pin3, IC1_pin8, IC2_pin2, IC2_pin3, IC2_pin8, IC2_pin11, IC3_pin2,
       IC3_pin3, IC3_pin8, IC3_pin11, IC4_pin1, IC4_pin2, IC4_pin3, IC4_pin8, IC4_pin11, IC15_pin10;
  wire [3:0] IC4_pin9, IC6_pin3, IC12_pin5, IC12_pin12, IC13_pin6, IC14_pin14, IC15_pin14, IC16_p10;

  _7474 IC4 (
    .pin1(IC4_pin1), .pin2(IC4_pin2), .pin3(IC4_pin3), .pin4(1'b1), .pin5(IC4_pin9[3]), .pin6(IC4_pin2),
    .pin7(1'b0), .pin8(IC4_pin8), .pin9(IC4_pin9[2]), .pin10(1'b1), .pin11(IC4_pin11), .pin12(IC4_pin8),
    .pin13(IC4_pin1), .pin14(1'b1));
  Button #(.activeLow("true")) CLEAR (.out(IC4_pin1));
  _74173 IC13 (
    .pin1(nOE), .pin2(nOE), .pin3(IC13_pin6[0]), .pin4(IC13_pin6[1]), .pin5(IC13_pin6[2]),
    .pin6(IC13_pin6[3]), .pin7(DEP), .pin8(1'b0), .pin9(HOLD_LD), .pin10(HOLD_LD), .pin11(IC4_pin9[3]),
    .pin12(IC4_pin9[2]), .pin13(IC4_pin9[1]), .pin14(IC4_pin9[0]), .pin15(CLR), .pin16(1'b1));
  _74173 IC12 (
    .pin1(nOE), .pin2(nOE), .pin3(IC12_pin5[0]), .pin4(IC12_pin5[1]), .pin5(IC12_pin5[2]),
    .pin6(IC12_pin5[3]), .pin7(DEP), .pin8(1'b0), .pin9(HOLD_LD), .pin10(HOLD_LD), .pin11(IC12_pin12[3]),
    .pin12(IC12_pin12[2]), .pin13(IC12_pin12[1]), .pin14(IC12_pin12[0]), .pin15(CLR), .pin16(1'b1));
  LED led_1 (.in(IC4_pin9[3]));
  _7474 IC3 (
    .pin1(IC4_pin1), .pin2(IC3_pin2), .pin3(IC3_pin3), .pin4(1'b1), .pin5(IC4_pin9[0]), .pin6(IC3_pin2),
    .pin7(1'b0), .pin8(IC3_pin8), .pin9(IC4_pin9[1]), .pin10(1'b1), .pin11(IC3_pin11), .pin12(IC3_pin8),
    .pin13(IC4_pin1), .pin14(1'b1));
  Button button_1 (.out(IC4_pin3));
  Seven_Seg_Hex seven_seg_hex_1 (.d(IC13_pin6), .dp(1'b0));
  LED led_2 (.in(IC4_pin9[2]));
  Button button_2 (.out(IC4_pin11));
  Seven_Seg_Hex seven_seg_hex_2 (.d(IC12_pin5), .dp(1'b0));
  LED led_3 (.in(IC4_pin9[1]));
  Button button_3 (.out(IC3_pin11));
  _74163 IC15 (
    .pin1(1'b1), .pin2(DEP), .pin3(IC13_pin6[0]), .pin4(IC13_pin6[1]), .pin5(IC13_pin6[2]),
    .pin6(IC13_pin6[3]), .pin7(1'b1), .pin8(1'b0), .pin9(LOAD), .pin10(IC15_pin10), .pin11(IC15_pin14[3]),
    .pin12(IC15_pin14[2]), .pin13(IC15_pin14[1]), .pin14(IC15_pin14[0]), .pin16(1'b1));  // open: pin15
  LED led_4 (.in(IC4_pin9[0]));
  _7474 IC2 (
    .pin1(IC4_pin1), .pin2(IC2_pin2), .pin3(IC2_pin3), .pin4(1'b1), .pin5(IC12_pin12[3]), .pin6(IC2_pin2),
    .pin7(1'b0), .pin8(IC2_pin8), .pin9(IC12_pin12[2]), .pin10(1'b1), .pin11(IC2_pin11), .pin12(IC2_pin8),
    .pin13(IC4_pin1), .pin14(1'b1));
  Button button_4 (.out(IC3_pin3));
  LED led_5 (.in(IC12_pin12[3]));
  Button button_5 (.out(IC2_pin3));
  LED led_6 (.in(IC12_pin12[2]));
  Button button_6 (.out(IC2_pin11));
  Seven_Seg_Hex seven_seg_hex_3 (.d(IC15_pin14), .dp(1'b0));
  LED led_7 (.in(IC12_pin12[1]));
  Button button_7 (.out(button_7_out));
  Seven_Seg_Hex seven_seg_hex_4 (.d(IC14_pin14), .dp(1'b0));
  _7474 IC1 (
    .pin1(IC4_pin1), .pin2(IC1_pin2), .pin3(IC1_pin3), .pin4(1'b1), .pin5(IC12_pin12[0]), .pin6(IC1_pin2),
    .pin7(1'b0), .pin8(IC1_pin8), .pin9(IC12_pin12[1]), .pin10(1'b1), .pin11(button_7_out), .pin12(IC1_pin8),
    .pin13(IC4_pin1), .pin14(1'b1));
  Seven_Seg_Hex seven_seg_hex_5 (.d(IC4_pin9), .dp(1'b0));
  LED led_8 (.in(IC12_pin12[0]));
  Button button_8 (.out(IC1_pin3));
  _74163 IC14 (
    .pin1(1'b1), .pin2(DEP), .pin3(IC12_pin5[0]), .pin4(IC12_pin5[1]), .pin5(IC12_pin5[2]),
    .pin6(IC12_pin5[3]), .pin7(1'b1), .pin8(1'b0), .pin9(LOAD), .pin10(1'b1), .pin11(IC14_pin14[3]),
    .pin12(IC14_pin14[2]), .pin13(IC14_pin14[1]), .pin14(IC14_pin14[0]), .pin15(IC15_pin10), .pin16(1'b1));
  Seven_Seg_Hex seven_seg_hex_6 (.d(IC12_pin12), .dp(1'b0));
  // A623308A IC16: pin names not known; wires that end beside it: in_7, IC15_pin14[3], IC15_pin14[2], IC15_pin14[1], IC15_pin14[0], IC14_pin14[3], IC14_pin14[2], IC14_pin14[1], IC14_pin14[0], IC16_p10[0], IC16_p10[1], IC16_p10[2], 1'b0, 1'b1, nWR, in_8, in_9, in_10, nRD, in_11, in_12, IC6_pin3[3]
  _74173 IC6 (
    .pin1(nOE_2), .pin2(nOE_2), .pin3(IC6_pin3[0]), .pin4(IC6_pin3[1]), .pin5(IC6_pin3[2]),
    .pin6(IC6_pin3[3]), .pin7(CK), .pin8(1'b0), .pin9(HOLD_LD_2), .pin10(HOLD_LD_2), .pin11(IC4_pin9[3]),
    .pin12(IC4_pin9[2]), .pin13(IC4_pin9[1]), .pin14(IC4_pin9[0]), .pin15(CLR_2), .pin16(1'b1));
  _74173 IC5 (
    .pin1(nOE_2), .pin2(nOE_2), .pin3(IC16_p10[0]), .pin4(IC16_p10[1]), .pin5(IC16_p10[2]),
    .pin6(IC16_p10[3]), .pin7(CK), .pin8(1'b0), .pin9(HOLD_LD_2), .pin10(HOLD_LD_2), .pin11(IC12_pin12[3]),
    .pin12(IC12_pin12[2]), .pin13(IC12_pin12[1]), .pin14(IC12_pin12[0]), .pin15(CLR_2), .pin16(1'b1));
  Seven_Seg_Hex seven_seg_hex_7 (.d(IC6_pin3), .dp(1'b0));
  Seven_Seg_Hex seven_seg_hex_8 (.d(IC16_p10), .dp(1'b0));

  // Notes on the sheet:
  //   Front Panel Interface
  //   ADDRESS
  //   DATA
endmodule
